# Fritzing sketch KY-006 (saved by Fritzing 0.9.4)

parts:
  Part1 = KY-006 Passive Buzzer Module [package="Breakout board"]
  Part2 = Arduino Uno (Rev3)

nets:
  N1: Part1.S, Part2.D8
  N2: Part1.-, Part2.GND

custom parts:
  KY-006 Passive Buzzer Module: Passive Piezoelectric Buzzer Module Keyes KY-006, it can produce a range of sound tones depending on the input frequency.
