# Fritzing sketch KY-011 (saved by Fritzing 0.9.4)
breadboards: 1

parts:
  Part1 = KY-011 Two Color LED Module [package="Breakout board"]
  Part2 = Arduino Uno (Rev3)
  R1 = Resistor [tolerance=±5% resistance=220 package="1206 [SMD]"]
  R2 = Resistor [tolerance=±5% resistance=220 package="2512 [SMD]"]

nets:
  N1: Part1.S, R2.Pin_0
  N2: Part1.Vin, R1.Pin_1
  N3: Part1.-, Part2.GND
  N4: Part2.D9_PWM, R2.Pin_1
  N5: Part2.D10_PWM/SS, R1.Pin_0

custom parts:
  KY-011 Two Color LED Module: KEYES KY-011 Two Color LED Module consist of a common cathode 3mm red/green LED.
