# Fritzing sketch final (saved by Fritzing 0.9.4)
breadboards: 1

parts:
  ZS-042_RTC1 = ZS-042 RTC Module
  Part2 = US-100 Ultrasonic Rangefinder
  Mod1 = Lipo Battery Pack
  Part3 = Solar Cell
  D1 = Rectifier Diode [package="Melf DO-213 AA [SMD]"]
  Part4 = Arduino Pro Mini (3.3V)
  Part5 = NRF24L01+ Breakout Board

nets:
  GND: ZS-042_RTC1.GND, Part2.GND, Part2.GND*, Mod1.GND, Part4.GND, Part5.GND
  VCC: ZS-042_RTC1.VCC, Part2.VCC, Mod1.3.3V, Part4.VCC, Part5.VCC
  N1: ZS-042_RTC1.SDA, Part4.A5
  N2: ZS-042_RTC1.SCL, Part4.A4
  N3: ZS-042_RTC1.SQW, Part4.D2
  N4: Mod1.?1, Part3.-
  N5: Mod1.?2, D1.cathode
  N6: Part3.+, D1.anode
  N7: Part4.SCK, Part5.SCK
  N8: Part4.MISO, Part5.MISO
  N9: Part4.MOSI, Part5.MOSI
  N10: Part4.D4, Part5.CS
  N11: Part4.D3, Part5.CE

custom parts:
  Lipo Battery Pack: Micro USB 5V 16340 18650 lithium Battery Shield V3 Wemos ESP32 ESP8266 Module
