# Fritzing sketch final (saved by Fritzing 0.9.4)
circuit board: 4.54481cm x 4.70529cm
circuit board: 8.46667cm x 5.64444cm
breadboards: 1

parts:
  Part9 = NRF24L01+ Breakout Board
  Part8 = Arduino Pro Mini (5V)
  C1 = Electrolytic Capacitor [capacitance=1µF package="100 mil [THT, electrolytic]"]
  ACS712_Current_Sensor1 = ACS712 Current Sensor
  ACS712_Current_Sensor2 = ACS712 Current Sensor
  ACS712_Current_Sensor3 = ACS712 Current Sensor
  ACS712_Current_Sensor4 = ACS712 Current Sensor
  JP1 = Header 6 [package=molex-1x6_lock]
  JP5 = Header 3 [package=screwterminal-3.5mm-3_lock.007s]
  JP2 = Header 3 [package=screwterminal-3.5mm-3_lock.007s]
  JP3 = Header 3 [package=screwterminal-3.5mm-3_lock.007s]
  JP4 = Header 3 [package=screwterminal-3.5mm-3_lock.007s]

nets:
  GND: Part9.GND, Part8.GND, C1.-, ACS712_Current_Sensor1.GND, ACS712_Current_Sensor2.GND, ACS712_Current_Sensor3.GND, ACS712_Current_Sensor4.GND
  VCC: Part9.VCC, Part8.VCC, C1.+, ACS712_Current_Sensor1.VCC, ACS712_Current_Sensor2.VCC, ACS712_Current_Sensor3.VCC, ACS712_Current_Sensor4.VCC
  N1: Part9.CE, Part8.D9
  N2: Part9.CS, Part8.D8
  N3: Part9.SCK, Part8.SCK
  N4: Part9.MOSI, Part8.MOSI
  N5: Part9.MISO, Part8.MISO
  N6: Part8.A3, ACS712_Current_Sensor3.OUT
  N7: Part8.A2, ACS712_Current_Sensor2.OUT
  N8: Part8.A1, ACS712_Current_Sensor4.OUT
  N9: Part8.A0, ACS712_Current_Sensor1.OUT
  N10: JP1.1, JP5.1, JP2.1, JP3.1, JP4.1
  N11: JP1.2, JP2.2
  N12: JP1.3, JP3.2
  N13: JP1.4, JP5.2
  N14: JP1.5, JP4.2
  N15: JP1.6, JP5.3, JP2.3, JP3.3, JP4.3

custom parts:
  ACS712 Current Sensor: A breakout board for the Allegro ACS712 is a Hall Effect-based linear current sensor. The module operates at 5V.
