# Fritzing sketch MQ5 (saved by Fritzing 0.9.4)
breadboards: 1

parts:
  Part2 = Arduino Uno (Rev3)
  Part3 = MQ-7 breakout

nets:
  N1: Part2.A0, Part3.AO
  N2: Part2.D3_PWM, Part3.DO
  5V: Part2.5V, Part3.VCC
  GND: Part2.GND, Part3.GND

custom parts:
  MQ-7 breakout: SKU: 101282
