# Fritzing sketch final (saved by Fritzing 0.9.4)

parts:
  Part1 = NRF24L01+ Breakout Board
  Part2 = Arduino Pro Mini (3.3V)
  Nokia_5110_LCD_Module1 = Nokia 5110 LCD
  U1 = ESP8266 WiFi Module [part_number=ESP8266]
  Part3 = KY-011 Two Color LED Module [package="Breakout board"]  # not connected
  Part4 = KY-006 Passive Buzzer Module [package="Breakout board"]  # not connected
  ZS-042_RTC1 = ZS-042 RTC Module
  microSD1 = MicroSD Card Module

nets:
  GND: Part1.GND, Part2.GND, Nokia_5110_LCD_Module1.GND, Nokia_5110_LCD_Module1.GND_(out), U1.GND, ZS-042_RTC1.GND, microSD1.GND
  VCC: Part1.VCC, Part2.VCC, Nokia_5110_LCD_Module1.VCC, Nokia_5110_LCD_Module1.VCC_(out), U1.VCC, ZS-042_RTC1.VCC, microSD1.VCC
  N1: Part2.A4, ZS-042_RTC1.SDA
  N2: Part2.A5, ZS-042_RTC1.SCL

custom parts:
  Nokia 5110 LCD: Nokia 5110 Graphic 84*48 LCD module such as the Sparkfun LCD-10168 or the clones from Ebay. There is example code for the Arduino available from the Sparkfun site in https://learn.sparkfun.com/tutorials/graphic-lcd-hookup-guide This is a 3.3V device, if you are running it from a 5V micro you need a 5V tolorant level translator such as the 74ahc367 to protect the signal imputs. Rafa G. did a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
  ESP8266 WiFi Module: Generic WiFi Module based on the ESP8266 with onboard PCB antenna and UART communications
  KY-011 Two Color LED Module: KEYES KY-011 Two Color LED Module consist of a common cathode 3mm red/green LED.
  KY-006 Passive Buzzer Module: Passive Piezoelectric Buzzer Module Keyes KY-006, it can produce a range of sound tones depending on the input frequency.
